// Logisim project Mux4Way16.circ as structural Verilog: 1 circuit, main circuit main
module main (
  input  [15:0] a,
  input  [15:0] b,
  input  [15:0] a_2,
  input  [15:0] c,
  input  [15:0] b_2,
  input  [15:0] d,
  input  [15:0] c_2,
  input  s1,
  input  s0,
  input  [15:0] d_2,
  input  s1_2,
  input  s0_2,
  output [15:0] out,
  output [15:0] out_2
);

  wire and_1_out, and_2_out, and_3_out, and_4_out, and_9_out, and_10_out, and_11_out, and_12_out, not_1_out,
       not_2_out, not_3_out, not_4_out, not_5_out, not_6_out, not_7_out, not_8_out;
  wire [15:0] and_5_out, and_6_out, and_7_out, and_8_out, and_13_out, and_14_out, and_15_out, and_16_out,
       bit_extender_1_out, bit_extender_2_out, bit_extender_3_out, bit_extender_4_out, bit_extender_5_out,
       bit_extender_6_out, bit_extender_7_out, bit_extender_8_out, or_1_out, or_2_out, or_4_out, or_5_out;

  not not_1 (not_1_out, s1_2);
  not not_2 (not_2_out, s0_2);
  not not_3 (not_3_out, s1_2);
  not not_4 (not_4_out, s0_2);
  and and_1 (and_1_out, not_1_out, not_2_out);
  and and_2 (and_2_out, not_3_out, s0_2);
  and and_3 (and_3_out, s1_2, not_4_out);
  and and_4 (and_4_out, s1_2, s0_2);
  assign bit_extender_1_out = {{15{and_1_out}}, and_1_out};  // Bit_Extender bit_extender_1
  assign bit_extender_2_out = {{15{and_2_out}}, and_2_out};  // Bit_Extender bit_extender_2
  assign bit_extender_3_out = {{15{and_3_out}}, and_3_out};  // Bit_Extender bit_extender_3
  assign bit_extender_4_out = {{15{and_4_out}}, and_4_out};  // Bit_Extender bit_extender_4
  assign and_5_out = a_2 & bit_extender_1_out;  // AND_Gate and_5, 16 bits wide
  assign and_6_out = b_2 & bit_extender_2_out;  // AND_Gate and_6, 16 bits wide
  assign and_7_out = c_2 & bit_extender_3_out;  // AND_Gate and_7, 16 bits wide
  assign and_8_out = d_2 & bit_extender_4_out;  // AND_Gate and_8, 16 bits wide
  assign or_1_out = and_5_out | and_6_out;  // OR_Gate or_1, 16 bits wide
  assign or_2_out = or_1_out | and_7_out;  // OR_Gate or_2, 16 bits wide
  assign out_2 = or_2_out | and_8_out;  // OR_Gate or_3, 16 bits wide
  not not_5 (not_5_out, s1);
  not not_6 (not_6_out, s0);
  not not_7 (not_7_out, s1);
  not not_8 (not_8_out, s0);
  and and_9 (and_9_out, not_5_out, not_6_out);
  and and_10 (and_10_out, not_7_out, s0);
  and and_11 (and_11_out, s1, not_8_out);
  and and_12 (and_12_out, s1, s0);
  assign bit_extender_5_out = {{15{and_9_out}}, and_9_out};  // Bit_Extender bit_extender_5
  assign bit_extender_6_out = {{15{and_10_out}}, and_10_out};  // Bit_Extender bit_extender_6
  assign bit_extender_7_out = {{15{and_11_out}}, and_11_out};  // Bit_Extender bit_extender_7
  assign bit_extender_8_out = {{15{and_12_out}}, and_12_out};  // Bit_Extender bit_extender_8
  assign and_13_out = a & bit_extender_5_out;  // AND_Gate and_13, 16 bits wide
  assign and_14_out = b & bit_extender_6_out;  // AND_Gate and_14, 16 bits wide
  assign and_15_out = c & bit_extender_7_out;  // AND_Gate and_15, 16 bits wide
  assign and_16_out = d & bit_extender_8_out;  // AND_Gate and_16, 16 bits wide
  assign or_4_out = and_13_out | and_14_out;  // OR_Gate or_4, 16 bits wide
  assign or_5_out = or_4_out | and_15_out;  // OR_Gate or_5, 16 bits wide
  assign out = or_5_out | and_16_out;  // OR_Gate or_6, 16 bits wide
endmodule
