// Logisim project Mux8Way16.circ as structural Verilog: 1 circuit, main circuit main
module main (
  input  [15:0] a,
  input  [15:0] b,
  input  [15:0] c,
  input  [15:0] d,
  input  [15:0] e,
  input  [15:0] f,
  input  [15:0] g,
  input  [15:0] h,
  input  s2,
  input  s1,
  input  s0,
  output [15:0] out
);

  wire and_1_out, and_2_out, and_3_out, and_4_out, and_5_out, and_6_out, and_7_out, and_8_out, not_1_out,
       not_2_out, not_3_out, not_4_out, not_5_out, not_6_out, not_7_out, not_8_out, not_9_out, not_10_out,
       not_11_out, not_12_out;
  wire [15:0] and_9_out, and_10_out, and_11_out, and_12_out, and_13_out, and_14_out, and_15_out, and_16_out,
       bit_extender_1_out, bit_extender_2_out, bit_extender_3_out, bit_extender_4_out, bit_extender_5_out,
       bit_extender_6_out, bit_extender_7_out, bit_extender_8_out;

  not not_1 (not_1_out, s2);
  not not_2 (not_2_out, s1);
  not not_3 (not_3_out, s0);
  not not_4 (not_4_out, s2);
  not not_5 (not_5_out, s1);
  not not_6 (not_6_out, s2);
  not not_7 (not_7_out, s0);
  not not_8 (not_8_out, s2);
  not not_9 (not_9_out, s1);
  not not_10 (not_10_out, s0);
  not not_11 (not_11_out, s1);
  not not_12 (not_12_out, s0);
  and and_1 (and_1_out, not_1_out, not_2_out, not_3_out);
  and and_2 (and_2_out, not_4_out, not_5_out, s0);
  and and_3 (and_3_out, not_6_out, s1, not_7_out);
  and and_4 (and_4_out, not_8_out, s1, s0);
  and and_5 (and_5_out, s2, not_9_out, not_10_out);
  and and_6 (and_6_out, s2, not_11_out, s0);
  and and_7 (and_7_out, s2, s1, not_12_out);
  and and_8 (and_8_out, s2, s1, s0);
  assign bit_extender_1_out = {{15{and_1_out}}, and_1_out};  // Bit_Extender bit_extender_1
  assign bit_extender_2_out = {{15{and_2_out}}, and_2_out};  // Bit_Extender bit_extender_2
  assign bit_extender_3_out = {{15{and_3_out}}, and_3_out};  // Bit_Extender bit_extender_3
  assign bit_extender_4_out = {{15{and_4_out}}, and_4_out};  // Bit_Extender bit_extender_4
  assign bit_extender_5_out = {{15{and_5_out}}, and_5_out};  // Bit_Extender bit_extender_5
  assign bit_extender_6_out = {{15{and_6_out}}, and_6_out};  // Bit_Extender bit_extender_6
  assign bit_extender_7_out = {{15{and_7_out}}, and_7_out};  // Bit_Extender bit_extender_7
  assign bit_extender_8_out = {{15{and_8_out}}, and_8_out};  // Bit_Extender bit_extender_8
  assign and_9_out = a & bit_extender_1_out;  // AND_Gate and_9, 16 bits wide
  assign and_10_out = b & bit_extender_2_out;  // AND_Gate and_10, 16 bits wide
  assign and_11_out = c & bit_extender_3_out;  // AND_Gate and_11, 16 bits wide
  assign and_12_out = d & bit_extender_4_out;  // AND_Gate and_12, 16 bits wide
  assign and_13_out = e & bit_extender_5_out;  // AND_Gate and_13, 16 bits wide
  assign and_14_out = f & bit_extender_6_out;  // AND_Gate and_14, 16 bits wide
  assign and_15_out = g & bit_extender_7_out;  // AND_Gate and_15, 16 bits wide
  assign and_16_out = h & bit_extender_8_out;  // AND_Gate and_16, 16 bits wide
  assign out = and_9_out | and_10_out | and_11_out | and_12_out | and_13_out | and_14_out | and_15_out | and_16_out;  // OR_Gate or_1, 16 bits wide
endmodule
