// Logisim project ALU.circ as structural Verilog: 1 circuit, main circuit main
module main (
  input  ZX,
  input  NX,
  input  ZY,
  input  NY,
  input  F,
  input  NO,
  input  [15:0] X,
  input  in_8,
  input  [15:0] Y,
  output [15:0] OUT
);

  wire not_6_out, or_1_out, or_2_out, or_3_out;
  wire [15:0] adder_1_out, and_1_out, and_2_out, and_3_out, bit_extender_1_out, bit_extender_2_out,
       multiplexer_1_out, multiplexer_2_out, multiplexer_3_out, not_1_out, not_2_out, not_3_out, not_4_out,
       not_5_out;

  assign bit_extender_1_out = {{15{ZX}}, ZX};  // Bit_Extender bit_extender_1
  assign not_1_out = ~bit_extender_1_out;  // NOT_Gate not_1, 16 bits wide
  assign and_1_out = not_1_out & X;  // AND_Gate and_1, 16 bits wide
  Multiplexer #(.width(16), .enable("false")) multiplexer_1 (
    .in0(and_1_out), .in1(not_2_out), .out(multiplexer_1_out), .sel(NX));
  assign not_2_out = ~and_1_out;  // NOT_Gate not_2, 16 bits wide
  assign bit_extender_2_out = {{15{ZY}}, ZY};  // Bit_Extender bit_extender_2
  assign not_3_out = ~bit_extender_2_out;  // NOT_Gate not_3, 16 bits wide
  assign and_2_out = not_3_out & Y;  // AND_Gate and_2, 16 bits wide
  assign not_4_out = ~and_2_out;  // NOT_Gate not_4, 16 bits wide
  Multiplexer #(.width(16), .enable("false")) multiplexer_2 (
    .in0(and_2_out), .in1(not_4_out), .out(multiplexer_2_out), .sel(NY));
  assign and_3_out = multiplexer_1_out & multiplexer_2_out;  // AND_Gate and_3, 16 bits wide
  Adder #(.width(16)) adder_1 (
    .a(multiplexer_1_out), .b(multiplexer_2_out), .out(adder_1_out), .cin(in_8));  // open: cout
  Multiplexer #(.width(16), .enable("false")) multiplexer_3 (
    .in0(and_3_out), .in1(adder_1_out), .out(multiplexer_3_out), .sel(F));
  Multiplexer #(.width(16), .enable("false")) multiplexer_4 (
    .in0(multiplexer_3_out), .in1(not_5_out), .out(OUT), .sel(NO));
  assign not_5_out = ~multiplexer_3_out;  // NOT_Gate not_5, 16 bits wide
  or or_1 (or_1_out, OUT[0], OUT[1], OUT[2], OUT[3], OUT[4], OUT[5], OUT[6], OUT[7]);
  or or_2 (or_2_out, OUT[8], OUT[9], OUT[10], OUT[11], OUT[12], OUT[13], OUT[14], OUT[15]);
  or or_3 (or_3_out, or_1_out, or_2_out);
  not not_6 (not_6_out, or_3_out);
  LED ZR (.in(not_6_out));
  LED NG (.in(OUT[15]));
endmodule
