// Logisim project HalfAdder.circ as structural Verilog: 1 circuit, main circuit main
module main (
  input  in_1,
  input  in_2
);

  wire and_1_out, xor_1_out;

  xor xor_1 (xor_1_out, in_1, in_2);
  and and_1 (and_1_out, in_1, in_2);
  LED Sum (.in(xor_1_out));
  LED Carry (.in(and_1_out));
endmodule
