// Logisim project Bit.circ as structural Verilog: 1 circuit, main circuit main
module main (
  input  load,
  input  in
);

  wire d_ff_1_q, multiplexer_1_out;

  Multiplexer #(.enable("false")) multiplexer_1 (.in0(d_ff_1_q), .in1(in), .out(multiplexer_1_out), .sel(load));
  D_Flip_Flop #(.trigger("high")) d_ff_1 (
    .clk(load), .D(multiplexer_1_out), .Q(d_ff_1_q));  // open: Qn, preset, en, reset
  LED out (.in(d_ff_1_q));
endmodule
