// Logisim project PC.circ as structural Verilog: 2 circuits, main circuit PC
module PC (
  input  inc,
  input  load,
  input  reset,
  input  in_4,
  input  [15:0] in,
  output [15:0] out
);

  wire [15:0] adder_1_out, multiplexer_1_out, multiplexer_2_out, multiplexer_3_out;

  Register register_1 (.in(multiplexer_3_out), .load(in_4), .out(out));
  Adder #(.width(16)) adder_1 (.a(out), .b(16'h1), .out(adder_1_out), .cin(1'b0));  // open: cout
  Multiplexer #(.width(16), .enable("false")) multiplexer_1 (
    .in0(out), .in1(adder_1_out), .out(multiplexer_1_out), .sel(inc));
  Multiplexer #(.width(16), .enable("false")) multiplexer_2 (
    .in0(multiplexer_1_out), .in1(in), .out(multiplexer_2_out), .sel(load));
  Multiplexer #(.width(16), .enable("false")) multiplexer_3 (
    .in0(multiplexer_2_out), .in1({16{1'b0}}), .out(multiplexer_3_out), .sel(reset));
endmodule

module Test (
  input  reset,
  input  load,
  input  inc,
  input  [15:0] in,
  output [15:0] out
);

  wire and_3_out, and_5_out, not_1_out, not_2_out, not_3_out;
  wire [15:0] adder_1_out, and_1_out, and_2_out, and_4_out, and_6_out, bit_extender_1_out,
       bit_extender_2_out, bit_extender_3_out, register_1_out;

  Register register_1 (.out(register_1_out));  // open: in, load
  assign and_1_out = register_1_out & {16{1'b0}};  // AND_Gate and_1, 16 bits wide
  Adder #(.width(16)) adder_1 (.a(register_1_out), .b(16'h1), .out(adder_1_out), .cin(1'b1));  // open: cout
  assign bit_extender_1_out = {{15{reset}}, reset};  // Bit_Extender bit_extender_1
  assign and_2_out = bit_extender_1_out & and_1_out;  // AND_Gate and_2, 16 bits wide
  not not_1 (not_1_out, reset);
  and and_3 (and_3_out, not_1_out, load);
  assign bit_extender_2_out = {{15{and_3_out}}, and_3_out};  // Bit_Extender bit_extender_2
  assign and_4_out = bit_extender_2_out & in;  // AND_Gate and_4, 16 bits wide
  not not_2 (not_2_out, reset);
  and and_5 (and_5_out, not_2_out, inc, not_3_out);
  not not_3 (not_3_out, load);
  assign bit_extender_3_out = {{15{and_5_out}}, and_5_out};  // Bit_Extender bit_extender_3
  assign and_6_out = bit_extender_3_out & adder_1_out;  // AND_Gate and_6, 16 bits wide
  assign out = and_2_out | and_4_out | and_6_out;  // OR_Gate or_1, 16 bits wide
endmodule
