// Logisim project RAM64.circ as structural Verilog: 1 circuit, main circuit RAM64
module RAM64 (
  input  load,
  input  [5:0] addres,
  input  [15:0] in,
  output [15:0] out
);

  wire and_1_out, and_2_out, and_3_out, and_4_out, and_5_out, and_6_out, and_7_out, and_8_out,
       demultiplexer_1_out0, demultiplexer_1_out1, demultiplexer_1_out2, demultiplexer_1_out3,
       demultiplexer_1_out4, demultiplexer_1_out5, demultiplexer_1_out6, demultiplexer_1_out7;
  wire [15:0] ram8_1_out, ram8_2_out, ram8_3_out, ram8_4_out, ram8_5_out, ram8_6_out, ram8_7_out, ram8_8_out;

  Demultiplexer #(.select(3), .enable("false")) demultiplexer_1 (
    .out0(demultiplexer_1_out0), .out1(demultiplexer_1_out1), .out2(demultiplexer_1_out2),
    .out3(demultiplexer_1_out3), .out4(demultiplexer_1_out4), .out5(demultiplexer_1_out5),
    .out6(demultiplexer_1_out6), .out7(demultiplexer_1_out7), .in(1'b1), .sel(addres[5:3]));
  and and_1 (and_1_out, demultiplexer_1_out0, load);
  and and_2 (and_2_out, demultiplexer_1_out1, load);
  and and_3 (and_3_out, demultiplexer_1_out2, load);
  and and_4 (and_4_out, demultiplexer_1_out3, load);
  and and_5 (and_5_out, demultiplexer_1_out4, load);
  and and_6 (and_6_out, demultiplexer_1_out5, load);
  and and_7 (and_7_out, demultiplexer_1_out6, load);
  and and_8 (and_8_out, demultiplexer_1_out7, load);
  RAM8 ram8_1 (.addres(addres[2:0]), .in(in), .load(and_1_out), .out(ram8_1_out));
  RAM8 ram8_2 (.addres(addres[2:0]), .in(in), .load(and_2_out), .out(ram8_2_out));
  RAM8 ram8_3 (.addres(addres[2:0]), .in(in), .load(and_3_out), .out(ram8_3_out));
  RAM8 ram8_4 (.addres(addres[2:0]), .in(in), .load(and_4_out), .out(ram8_4_out));
  RAM8 ram8_5 (.addres(addres[2:0]), .in(in), .load(and_5_out), .out(ram8_5_out));
  RAM8 ram8_6 (.addres(addres[2:0]), .in(in), .load(and_6_out), .out(ram8_6_out));
  RAM8 ram8_7 (.addres(addres[2:0]), .in(in), .load(and_7_out), .out(ram8_7_out));
  RAM8 ram8_8 (.addres(addres[2:0]), .in(in), .load(and_8_out), .out(ram8_8_out));
  Multiplexer #(.select(3), .width(16), .enable("false")) multiplexer_1 (
    .in0(ram8_1_out), .in1(ram8_2_out), .in2(ram8_3_out), .in3(ram8_4_out), .in4(ram8_5_out),
    .in5(ram8_6_out), .in6(ram8_7_out), .in7(ram8_8_out), .out(out), .sel(addres[5:3]));
endmodule
