// Logisim project CPU.circ as structural Verilog: 1 circuit, main circuit CPU
module CPU (
  input  [15:0] instruction,
  input  [15:0] inM,
  input  reset,
  output [15:0] outM,
  output writeM,
  output [15:0] addressM,
  output [15:0] pc
);

  wire alu_1_ng, alu_1_zr, and_1_out, and_2_out, and_3_out, and_4_out, and_5_out, multiplexer_2_out,
       multiplexer_3_out, not_1_out, not_2_out, or_1_out;
  wire [15:0] D_out, multiplexer_1_out, multiplexer_4_out;

  Multiplexer #(.width(16), .enable("false")) multiplexer_1 (
    .in0(instruction), .in1(outM), .out(multiplexer_1_out), .sel(instruction[15]));
  Multiplexer #(.enable("false")) multiplexer_2 (
    .in0(1'b1), .in1(instruction[5]), .out(multiplexer_2_out), .sel(instruction[15]));
  Register A (.in(multiplexer_1_out), .load(multiplexer_2_out), .out(addressM));
  Multiplexer #(.enable("false")) multiplexer_3 (
    .in0(1'b0), .in1(instruction[4]), .out(multiplexer_3_out), .sel(instruction[15]));
  Register D (.in(outM), .load(multiplexer_3_out), .out(D_out));
  Multiplexer #(.width(16), .enable("false")) multiplexer_4 (
    .in0(addressM), .in1(inM), .out(multiplexer_4_out), .sel(instruction[12]));
  and and_1 (and_1_out, instruction[2], alu_1_ng);
  and and_2 (and_2_out, instruction[1], alu_1_zr);
  or or_1 (or_1_out, and_1_out, and_2_out, and_4_out);
  and and_3 (and_3_out, instruction[15], or_1_out);
  PC pc_1 (.in(addressM), .out(pc), .inc(1'b1), .load(and_3_out), .reset(reset));
  not not_1 (not_1_out, alu_1_ng);
  and and_4 (and_4_out, instruction[0], and_5_out);
  not not_2 (not_2_out, alu_1_zr);
  and and_5 (and_5_out, not_1_out, not_2_out);
  ALU alu_1 (
    .X(D_out), .Y(multiplexer_4_out), .OUT(outM), .ZX(instruction[11]), .NX(instruction[10]),
    .ZY(instruction[9]), .NY(instruction[8]), .F(instruction[7]), .NO(instruction[6]), .ZR(alu_1_zr),
    .NG(alu_1_ng));
  and and_6 (writeM, instruction[3], instruction[15]);
endmodule
